# Fritzing sketch circuit (saved by Fritzing 1.0.8)
breadboards: 1

parts:
  Raspberry_Pi = Raspberry Pi 3 [part_number=RPI-3-V1.2]
  B0 = Pushbutton [package=THT]
  B1 = Pushbutton [package=THT]
  B2 = Pushbutton [package=THT]
  B3 = Pushbutton [package=THT]
  A0 = Pushbutton [package=THT]
  A1 = Pushbutton [package=THT]
  A2 = Pushbutton [package=THT]
  A3 = Pushbutton [package=THT]
  S3 = LED - 5mm [color="Red (633nm)" current=0.030A package="5 mm [THT]"]
  S2 = LED - 5mm [color="Red (633nm)" current=0.030A package="5 mm [THT]"]
  S1 = LED - 5mm [color="Red (633nm)" current=0.030A package="5 mm [THT]"]
  S0 = LED - 5mm [color="Red (633nm)" current=0.030A package="5 mm [THT]"]
  C4 = LED - 5mm [color="Green (560nm)" current=0.030A package="5 mm [THT]"]
  R1 = Resistor [tolerance=±5% power=0.25W resistance=220 package=THT]
  R2 = Resistor [tolerance=±5% power=0.25W resistance=220 package=THT]
  R3 = Resistor [tolerance=±5% power=0.25W resistance=220 package=THT]
  R4 = Resistor [tolerance=±5% power=0.25W resistance=220 package=THT]
  R5 = Resistor [tolerance=±5% power=0.25W resistance=220 package=THT]
  R6 = Resistor [tolerance=±5% power=0.25W resistance=10k package=THT]
  R7 = Resistor [tolerance=±5% power=0.25W resistance=10k package=THT]
  R8 = Resistor [tolerance=±5% power=0.25W resistance=10k package=THT]
  R9 = Resistor [tolerance=±5% power=0.25W resistance=10k package=THT]
  R10 = Resistor [tolerance=±5% power=0.25W resistance=10k package=THT]
  R11 = Resistor [tolerance=±5% power=0.25W resistance=10k package=THT]
  R12 = Resistor [tolerance=±5% power=0.25W resistance=10k package=THT]
  R13 = Resistor [tolerance=±5% power=0.25W resistance=10k package=THT]

nets:
  3V3: Raspberry_Pi.3v3, Raspberry_Pi.3V3, B0.leg1, B1.leg1, B2.leg1, B3.leg1, A0.leg1, A1.leg1, A2.leg1, A3.leg1, R6.Pin_1, R7.Pin_1, R8.Pin_1, R9.Pin_1, R10.Pin_1, R11.Pin_1, R12.Pin_1, R13.Pin_1
  N1: Raspberry_Pi.GPIO2, A0.leg0
  N2: Raspberry_Pi.GPIO3, A1.leg0
  N3: Raspberry_Pi.GIPO4, A2.leg0
  N4: Raspberry_Pi.GIPO17, A3.leg0
  N5: Raspberry_Pi.GIPO27, B0.leg0
  N6: Raspberry_Pi.GIPO22, B1.leg0
  N7: Raspberry_Pi.GIPO10, B2.leg0
  N8: Raspberry_Pi.GIPO9, B3.leg0
  N9: Raspberry_Pi.GIPO11, S0.anode
  N10: Raspberry_Pi.GIPO5, S1.anode
  N11: Raspberry_Pi.GIPO6, S2.anode
  N12: Raspberry_Pi.GIPO13, S3.anode
  N13: Raspberry_Pi.GIPO19, C4.anode
  N14: Raspberry_Pi.GND, R1.Pin_1, R2.Pin_1, R3.Pin_1, R4.Pin_1, R5.Pin_1, R6.Pin_0, R7.Pin_0, R8.Pin_0, R9.Pin_0, R10.Pin_0, R11.Pin_0, R12.Pin_0, R13.Pin_0
  N15: S3.cathode, R2.Pin_0
  N16: S2.cathode, R3.Pin_0
  N17: S1.cathode, R4.Pin_0
  N18: S0.cathode, R5.Pin_0
  N19: C4.cathode, R1.Pin_0

notes:
  B3, B2, B1, B0
  A3, A2, A1, A0
  C4, S3, S2, S1, S0
