# Fritzing sketch pi-4-bit-adder (saved by Fritzing 1.0.8)
breadboards: 1

parts:
  S2 = LED - 5mm [color="Red (633nm)" current=0.030A package="5 mm [THT]"]
  S0 = LED - 5mm [color="Red (633nm)" current=0.030A package="5 mm [THT]"]
  R6 = Resistor [tolerance=±5% power=0.25W resistance=15k package=THT]
  C4 = LED - 5mm [color="Green (560nm)" current=0.030A package="5 mm [THT]"]
  B3 = Pushbutton [package="[THT]"]
  R8 = Resistor [tolerance=±5% power=0.25W resistance=15k package=THT]
  R12 = Resistor [tolerance=±5% power=0.25W resistance=15k package=THT]
  S3 = LED - 5mm [color="Red (633nm)" current=0.030A package="5 mm [THT]"]
  R4 = Resistor [tolerance=±5% power=0.25W resistance=220 package=THT]
  R10 = Resistor [tolerance=±5% power=0.25W resistance=15k package=THT]
  R1 = Resistor [tolerance=±5% power=0.25W resistance=220 package=THT]
  R13 = Resistor [tolerance=±5% power=0.25W resistance=15k package=THT]
  R2 = Resistor [tolerance=±5% power=0.25W resistance=220 package=THT]
  A1 = Pushbutton [package="[THT]"]
  B0 = Pushbutton [package="[THT]"]
  A0 = Pushbutton [package="[THT]"]
  Raspberry_Pi = Raspberry Pi 3 [part_number=RPI-3-V1.2]
  B1 = Pushbutton [package="[THT]"]
  R3 = Resistor [tolerance=±5% power=0.25W resistance=220 package=THT]
  R11 = Resistor [tolerance=±5% power=0.25W resistance=15k package=THT]
  R5 = Resistor [tolerance=±5% power=0.25W resistance=220 package=THT]
  A3 = Pushbutton [package="[THT]"]
  S1 = LED - 5mm [color="Red (633nm)" current=0.030A package="5 mm [THT]"]
  A2 = Pushbutton [package="[THT]"]
  R7 = Resistor [tolerance=±5% power=0.25W resistance=15k package=THT]
  B2 = Pushbutton [package="[THT]"]
  R9 = Resistor [tolerance=±5% power=0.25W resistance=15k package=THT]

nets:
  N1: S2.cathode, R3.Pin_1
  N2: S2.anode, Raspberry_Pi.GIPO6
  N3: S0.cathode, R5.Pin_1
  N4: S0.anode, Raspberry_Pi.GIPO11
  N5: R6.Pin_0, A0.Pin_1, A0.Pin_2, Raspberry_Pi.GIPO23
  N6: R6.Pin_1, R8.Pin_1, R12.Pin_1, R4.Pin_0, R10.Pin_1, R1.Pin_0, R13.Pin_1, R2.Pin_0, Raspberry_Pi.GND, R3.Pin_0, R11.Pin_1, R5.Pin_0, R7.Pin_1, R9.Pin_1
  N7: C4.cathode, R1.Pin_1
  N8: C4.anode, Raspberry_Pi.GIPO19
  N9: B3.Pin_1, B3.Pin_2, R13.Pin_0, Raspberry_Pi.GIPO9
  3V3: B3.Pin_3, B3.Pin_4, A1.Pin_3, A1.Pin_4, B0.Pin_3, B0.Pin_4, A0.Pin_3, A0.Pin_4, Raspberry_Pi.3v3, Raspberry_Pi.3V3, B1.Pin_3, B1.Pin_4, A3.Pin_3, A3.Pin_4, A2.Pin_3, A2.Pin_4, B2.Pin_3, B2.Pin_4
  N10: R8.Pin_0, Raspberry_Pi.GIPO4, A2.Pin_1, A2.Pin_2
  N11: R12.Pin_0, Raspberry_Pi.GIPO10, B2.Pin_1, B2.Pin_2
  N12: S3.cathode, R2.Pin_1
  N13: S3.anode, Raspberry_Pi.GIPO13
  N14: R4.Pin_1, S1.cathode
  N15: R10.Pin_0, B0.Pin_1, B0.Pin_2, Raspberry_Pi.GIPO27
  N16: A1.Pin_1, A1.Pin_2, Raspberry_Pi.GIPO24, R7.Pin_0
  N17: Raspberry_Pi.GIPO17, A3.Pin_1, A3.Pin_2, R9.Pin_0
  N18: Raspberry_Pi.GIPO22, B1.Pin_1, B1.Pin_2, R11.Pin_0
  N19: Raspberry_Pi.GIPO5, S1.anode

notes:
  B3, B2, B1, B0
  A3, A2, A1, A0
  C4, S3, S2, S1, S0
